# Fritzing sketch MysteryMachine2Standalone (saved by Fritzing 0.9.3b)
circuit board: 16cm x 10cm
breadboards: 3

parts:
  SR2 = Mystery Part - 16 pins [chip_label=SN74HC595 package=THT]
  SR1 = Mystery Part - 16 pins [chip_label=SN74HC595 package=THT]
  LED_2_3 = LED - 5mm [color="Yellow (595nm)" package="5 mm [THT]"]
  LED_2_5 = LED - 5mm [color="Blue (525nm)" package="5 mm [THT]"]
  LED_2_4 = LED - 5mm [color="Green (565nm)" package="5 mm [THT]"]
  LED_2_2 = LED - 5mm [color="Orange (620nm)" package="5 mm [THT]"]
  LED_2_1 = LED - 5mm [color="Red (633nm)" package="5 mm [THT]"]
  RT_2 = Resistor [tolerance=±5% resistance=1M package=THT]
  Touch2 = Resistor [tolerance=±5% resistance=0 package=THT]
  LED_1_3 = LED - 5mm [color="Yellow (595nm)" package="5 mm [THT]"]
  LED_1_5 = LED - 5mm [color="Blue (525nm)" package="5 mm [THT]"]
  LED_1_1 = LED - 5mm [color="Red (633nm)" package="5 mm [THT]"]
  LED_1_4 = LED - 5mm [color="Green (565nm)" package="5 mm [THT]"]
  LED_1_2 = LED - 5mm [color="Orange (620nm)" package="5 mm [THT]"]
  RT_1 = Resistor [tolerance=±5% resistance=1M package=THT]
  Touch1 = Resistor [tolerance=±5% resistance=0 package=THT]
  LEDM_1 = LED - 5mm [color="Red (633nm)" package="5 mm [THT]"]
  LEDM_2 = LED - 5mm [color="Red (633nm)" package="5 mm [THT]"]
  LEDM_3 = LED - 5mm [color="Red (633nm)" package="5 mm [THT]"]
  TouchMid = Resistor [tolerance=±5% resistance=0 package=THT]
  RT_M = Resistor [tolerance=±5% resistance=1M package=THT]
  R1 = Resistor [tolerance=±5% resistance=330 package=THT]
  RM = Resistor [tolerance=±5% resistance=330 package=THT]
  R2 = Resistor [tolerance=±5% resistance=330 package=THT]
  Y2 = CRYSTAL [package=crystal-smd-10.5x4.8-2pin]
  VCC2 = 4 x AAA Battery Mount
  C5 = Capacitor [package=cap-pth-small2]
  C4 = Capacitor [package=cap-pth-small2]
  U3 = atmega328 [package=dip]

nets (from the breadboard view):
  N1: SR2.pin1, LED_2_2.anode
  N2: SR2.pin2, LED_2_3.anode
  N3: SR2.pin3, LED_2_4.anode
  N4: SR2.pin4, LED_2_5.anode
  N5: SR2.pin8, SR2.pin13, SR1.pin8, SR1.pin13, R1.Pin_0, RM.Pin_0, R2.Pin_0, VCC2.-, C5.2, C4.2, U3.GND
  N6: SR2.pin10, SR2.pin16, SR1.pin10, SR1.pin16, VCC2.+, U3.VCC, U3.AVCC, U3.AREF
  N7: SR2.pin11, SR1.pin11, U3.D4
  N8: SR2.pin12, SR1.pin12, U3.D3_(PWM)
  N9: SR2.pin14, SR1.pin9
  N10: SR2.pin15, LED_2_1.anode
  N11: SR1.pin1, LEDM_2.anode
  N12: SR1.pin2, LEDM_3.anode
  N13: SR1.pin3, LED_1_1.anode
  N14: SR1.pin4, LED_1_2.anode
  N15: SR1.pin5, LED_1_3.anode
  N16: SR1.pin6, LED_1_4.anode
  N17: SR1.pin7, LED_1_5.anode
  N18: SR1.pin14, U3.D2
  N19: SR1.pin15, LEDM_1.anode
  N20: LED_2_3.cathode, LED_2_5.cathode, LED_2_4.cathode, LED_2_2.cathode, LED_2_1.cathode, R2.Pin_1
  N21: RT_2.Pin_0, U3.D9_(PWM)
  N22: RT_2.Pin_1, Touch2.Pin_1, U3.D8
  N23: LED_1_3.cathode, LED_1_5.cathode, LED_1_1.cathode, LED_1_4.cathode, LED_1_2.cathode, R1.Pin_1
  N24: RT_1.Pin_0, Touch1.Pin_1, U3.D6_(PWM)
  N25: RT_1.Pin_1, U3.D7
  N26: LEDM_1.cathode, LEDM_2.cathode, LEDM_3.cathode, RM.Pin_1
  N27: TouchMid.Pin_1, RT_M.Pin_0, U3.D10_(PWM)
  N28: RT_M.Pin_1, U3.D11_(PWM)
  N29: Y2.1, C4.1, U3.XLAT1
  N30: Y2.2, C5.1, U3.XLAT2

notes:
  Blue = Arduino D2 = data pin = SER of SN74HC595
  Yellow = Arduino D3 = latch pin = RCLK of SN74HC595
  Green = Arduino D4 = clock pin = SRCLK of SN74HC595
  Orange = daisy chain
  SN74HC595
  16 15 14 13 12 11 10 9
  | | | | | | | |
  +--+--+--+--+--+--+--+
  |> |
  +--+--+--+--+--+--+--+
  | | | | | | | |
  1 2 3 4 5 6 7 8
  Officiele pin namen:
  1: Q2
  2: Q3
  3: Q4
  3: Q5
  5: Q6
  6: Q7
  7: Q8
  8: GND
  9: QH* (voor daisy chaining)
  10: SRCLR* (naar 5V)
  11: SRCLK (naar D4): clock pin
  12: RCLK (naar D3): latch pin
  13: OE* (naar GND)
  14: SER (naar D2): data pin
  15: Q1
  16: VCC (naar 5V)
  SN74HC595
  16 15 14 13 12 11 10 9
  | | | | | | | |
  +--+--+--+--+--+--+--+
  |> |
  +--+--+--+--+--+--+--+
  | | | | | | | |
  1 2 3 4 5 6 7 8
  Verbindingen:
  1: LED 2
  2: LED 3
  3: LED 4
  3: LED 5
  5: LED 6
  6: LED 7
  7: LED 8
  8: GND
  9: daisy chaining
  10: naar 5V
  11: naar D4: clock pin
  12: naar D3: latch pin
  13: naar GND
  14: naar D2: data pin
  15: naar LED1
  16: naar 5V
  const int datapin = 2;
  const int latchpin = 3;
  const int clockpin = 4;
  void setup()
  {
  pinMode(datapin, OUTPUT);
  pinMode(latchpin, OUTPUT);
  pinMode(clockpin, OUTPUT);
  }
  void loop()
  {
  for (byte i=0; i!=256; ++i)
  {
  //Laat het getal i als binair zien
  ShowBinary(i);
  delay(100);
  }
  }
  void ShowBinary(const byte getal)
  {
  // Stuur de data naar het shift register
  shiftOut(datapin, clockpin, MSBFIRST, getal);
  // Zet de latch aan en uit, zodat de outputs aan gaan
  digitalWrite(latchpin, HIGH);
  digitalWrite(latchpin, LOW);
  }
  Capacitors: 22 pF
  Crystal: 16 MHz

custom parts:
  Mystery Part - 16 pins: A dummy, proxy, ersatz, stand-in part for whatever you want. With 16 pins on a 300mil inline pin header footprint.
