# Fritzing sketch MysteryMachine2 (saved by Fritzing 0.8.5b)
circuit board: 16cm x 10cm
breadboards: 2

parts:
  R_LC = Resistor [tolerance=±5% resistance=1k package=THT]
  T1 = Toggle Switch [package=THT]
  T2 = Toggle Switch [package=THT]
  RotSwitch1 = female pin header, 6 pins [form="♀ (female)"]
  R1_1 = Resistor [tolerance=±5% resistance=10k package=THT]
  R1_3 = Resistor [tolerance=±5% resistance=10k package=THT]
  R1_4 = Resistor [tolerance=±5% resistance=10k package=THT]
  R1_5 = Resistor [tolerance=±5% resistance=10k package=THT]
  R_L1 = Resistor [tolerance=±5% resistance=1k package=THT]
  R1_2 = Resistor [tolerance=±5% resistance=10k package=THT]
  RotSwitch2 = female pin header, 6 pins [form="♀ (female)"]
  R2_1 = Resistor [tolerance=±5% resistance=10k package=THT]
  R_L2 = Resistor [tolerance=±5% resistance=1k package=THT]
  R2_4 = Resistor [tolerance=±5% resistance=10k package=THT]
  R2_5 = Resistor [tolerance=±5% resistance=10k package=THT]
  R2_2 = Resistor [tolerance=±5% resistance=10k package=THT]
  R2_3 = Resistor [tolerance=±5% resistance=10k package=THT]
  S1 = Pushbutton [package="[THT]"]
  S2 = Pushbutton [package="[THT]"]
  L2_6 = LED - 5mm [color="Red (633nm)" package="5 mm [THT]"]
  L1_6 = LED - 5mm [color="Red (633nm)" package="5 mm [THT]"]
  L2_7 = LED - 5mm [color="Orange (612nm)" package="5 mm [THT]"]
  L1_7 = LED - 5mm [color="Orange (612nm)" package="5 mm [THT]"]
  L2_8 = LED - 5mm [color="Green (565nm)" package="5 mm [THT]"]
  L1_8 = LED - 5mm [color="Green (565nm)" package="5 mm [THT]"]
  L2_9 = LED - 5mm [color="Yellow (585nm)" package="5 mm [THT]"]
  L1_9 = LED - 5mm [color="Yellow (585nm)" package="5 mm [THT]"]
  L2_10 = LED - 5mm [color="Blue (505nm)" package="5 mm [THT]"]
  L1_10 = LED - 5mm [color="Blue (505nm)" package="5 mm [THT]"]
  L_3 = LED - 5mm [color="Red (633nm)" package="5 mm [THT]"]
  L_Mid1 = LED - 5mm [color="Red (633nm)" package="5 mm [THT]"]
  L_4 = LED - 5mm [color="Red (633nm)" package="5 mm [THT]"]
  U2 = atmega328 [package=dip]
  C4 = Capacitor [package=cap-pth-small2]
  C5 = Capacitor [package=cap-pth-small2]
  Y2 = CRYSTAL [package=crystal-smd-10.5x4.8-2pin]
  VCC2 = 4 x AAA Battery Mount
  Part1 = Arduino Uno (Rev3)
  J_Battery = female pin header, 2 pins [form="♀ (female)"]

nets:
  N1: R_LC.Pin_0, L_3.cathode, L_Mid1.cathode, L_4.cathode
  N2: R_LC.Pin_1, T2.COM, RotSwitch1.pin6, R1_1.Pin_1, R1_3.Pin_1, R1_4.Pin_1, R1_5.Pin_1, R_L1.Pin_1, R1_2.Pin_1, RotSwitch2.pin6, R2_1.Pin_1, R_L2.Pin_1, R2_4.Pin_1, R2_5.Pin_1, R2_2.Pin_1, R2_3.Pin_1, S1.Pin_3, S1.Pin_4, S2.Pin_1, S2.Pin_2, Part1.GND
  N3: T1.L1, T2.L1
  N4: T1.COM, Part1.5V
  N5: T1.L2, T2.L2
  N6: RotSwitch1.pin1, R1_1.Pin_0, L1_6.anode, U2.D2, Part1.D2
  N7: RotSwitch1.pin2, R1_2.Pin_0, L1_7.anode, U2.D3_(PWM), Part1.D3_PWM
  N8: RotSwitch1.pin3, R1_3.Pin_0, L1_9.anode, U2.D4, Part1.D4
  N9: RotSwitch1.pin4, R1_4.Pin_0, L1_8.anode, U2.D5_(PWM), Part1.D5_PWM
  N10: RotSwitch1.pin5, R1_5.Pin_0, L1_10.anode, U2.D6_(PWM), Part1.D6_PWM
  N11: R_L1.Pin_0, L1_6.cathode, L1_7.cathode, L1_8.cathode, L1_9.cathode, L1_10.cathode
  N12: RotSwitch2.pin1, R2_1.Pin_0, L2_6.anode, U2.D8, Part1.D8
  N13: RotSwitch2.pin2, R2_2.Pin_0, L2_7.anode, U2.D9_(PWM), Part1.D9_PWM
  N14: RotSwitch2.pin3, R2_3.Pin_0, L2_9.anode, U2.D10_(PWM), Part1.D10_PWM/SS
  N15: RotSwitch2.pin4, R2_4.Pin_0, L2_8.anode, U2.D11_(PWM), Part1.D11_PWM/MOSI
  N16: RotSwitch2.pin5, R2_5.Pin_0, L2_10.anode, U2.D12, Part1.D12/MISO
  N17: R_L2.Pin_0, L2_6.cathode, L2_7.cathode, L2_8.cathode, L2_9.cathode, L2_10.cathode
  N18: S1.Pin_1, S1.Pin_2, S2.Pin_3, S2.Pin_4
  N19: L_3.anode, U2.A2, Part1.A2
  N20: L_Mid1.anode, U2.A1, Part1.A1
  N21: L_4.anode, U2.A0, Part1.A0
  N22: U2.VCC, U2.AVCC, U2.AREF, VCC2.+, J_Battery.pin1
  N23: U2.GND#7, C4.1, C5.2, VCC2.-, J_Battery.pin2
  N24: U2.XLAT1, C4.2, Y2.2
  N25: U2.XLAT2, C5.1, Y2.1

notes:
  The monopolar rotary switch is connected as such:
  1: Red, RS_1, A0/8
  2: Orange, RS_2, A1/9
  3: Yellow, RS_3, A2/10
  4: Green, RS_4, A3/11
  5: Cyan, RS_5, A4/12
  6: +5V, RS_A (the pole)
  Goals are
  (1) supply an LED with power, bypassing the Arduino
  (2) let the Arduino detect which choice is made
  Of these three LEDs, one will be turned on, when both pushbuttons are pressed
  Below is the alternative wiring for a bare-bones version
  Capacitors: 22 pF
  Crystal: 16 MHz
  General pins board
  1: D1
  ...
  13: D13
  14: A0
  ...
  18: A4
  19: 5V
  20: GND
